# Fritzing sketch temp_humid_schematic (saved by Fritzing 0.8.7b)

parts:
  Part1 = Arduino Uno (Rev3)
  LCD1 = LCD screen
  DHT2 = DHT11 Humitidy and Temperature Sensor
  T1 = LM35 Temperature Sensor [package="TO92 [THT]"]
  U1 = POT [package=pot_alpha_rv16af-20]

nets:
  N1: Part1.A5/SCL, T1.Vout
  N2: Part1.D8, LCD1.E
  N3: Part1.D9_PWM, LCD1.RS
  GND: Part1.GND, DHT2.GND, T1.GND
  N4: Part1.D2, DHT2.DATA
  N5: Part1.D3_PWM, LCD1.DB6
  N6: Part1.D4, LCD1.DB5
  N7: Part1.D5_PWM, LCD1.DB4
  N8: Part1.D6_PWM, LCD1.DB7
  5V: Part1.5V, DHT2.VDD
  N9: LCD1.V0, U1.S

custom parts:
  DHT11 Humitidy and Temperature Sensor: DHT11 Humidity and Temperature Sensor
